# Fritzing sketch tutorial (saved by Fritzing 0.9.6b)
breadboards: 1

parts:
  Part1 = ws2812b [package="smd 2812b"]
  Part2 = ws2812b [package="smd 2812b"]
  Part3 = ws2812b [package="smd 2812b"]
  Part4 = ws2812b [package="smd 2812b"]

nets:
  VDD: Part1.VDD, Part2.VDD, Part3.VDD, Part4.VDD
  N1: Part1.DOUT, Part2.DIN
  VSS: Part1.VSS, Part2.VSS, Part3.VSS, Part4.VSS
  N2: Part2.DOUT, Part3.DIN
  N3: Part3.DOUT, Part4.DIN
