# Fritzing sketch breadboard (saved by Fritzing 1.0.1rc)
breadboards: 1

parts:
  LED1 = LED - 5mm [color="Red (633nm)" current=0.030 package="5 mm [THT]"]
  A1 = Raspberry Pi Pico W
  V1 = DC Power [voltage=5]
  V2 = DC Power [voltage=5]
  RGB_SMD_LED1 = SMD RGB LED (WS2812) [package=5050]
  RGB_SMD_LED4 = SMD RGB LED (WS2812) [package=5050]
  R1 = Resistor [tolerance=±5% power=0.25 resistance=330 package=THT]
  J1 = female pin header, 3 pins [form="♀ (female)"]
  J4 = female pin header, 3 pins [form="♀ (female)"]
  S3 = Pushbutton [package="[THT]"]

nets:
  N1: LED1.cathode, A1.pin_3, A1.pin_8, A1.pin_13, A1.pin_18, A1.pin_23, A1.pin_28, A1.pin_33, A1.pin_38, V1.V-, S3.Pin_1, S3.Pin_2
  N2: LED1.anode, R1.Pin_1
  N3: A1.pin_20, RGB_SMD_LED1.DIn, J1.pin2
  N4: A1.pin_21, RGB_SMD_LED4.DIn, J4.pin2
  N5: A1.pin_29, R1.Pin_0
  N6: A1.pin_30, S3.Pin_3, S3.Pin_4
  N7: A1.pin_40, V1.V+
  VCC: V2.V+, RGB_SMD_LED1.VCC, RGB_SMD_LED4.VCC, J1.pin1, J4.pin1
  VSS: V2.V-, RGB_SMD_LED1.VSS, RGB_SMD_LED4.VSS, J1.pin3, J4.pin3

notes:
  Separate supplies for the Pico and the neopixels are highly recommended

custom parts:
  Raspberry Pi Pico W: Raspberry Pi Pico W. Based around the RP2040 microcontroller the Pico W is a low cost microcontroller device bringing Raspberry Pi quality, cost, and easy of use to the microcontroller space. The areas marked KEEPOUT in pcb silkscreen should not have traces running through them to avoid shorts on a soldered in module!
